// Logisim project main.circ as structural Verilog: 28 circuits, main circuit TwoBitAdder
module TwoBitAdder (
  input  [1:0] A,
  input  [1:0] B,
  input  C_in,
  output [1:0] Sum,
  output C_out
);

  wire and_1_out, and_2_out, and_3_out, and_4_out, or_1_out, xor_1_out, xor_3_out;

  xor xor_1 (xor_1_out, A[0], B[0]);
  xor xor_2 (Sum[0], xor_1_out, C_in);
  and and_1 (and_1_out, xor_1_out, C_in);
  and and_2 (and_2_out, A[0], B[0]);
  or or_1 (or_1_out, and_1_out, and_2_out);
  xor xor_3 (xor_3_out, A[1], B[1]);
  xor xor_4 (Sum[1], xor_3_out, or_1_out);
  and and_3 (and_3_out, xor_3_out, or_1_out);
  and and_4 (and_4_out, A[1], B[1]);
  or or_2 (C_out, and_3_out, and_4_out);

  // Notes on the sheet:
  //   External Carry
  //   S1
  //   Two Bit Adder
  //   B1
  //   B2
  //   S2
  //   Carry-out
endmodule

module FourBitAdder (
  input  [3:0] A,
  input  [3:0] B,
  input  C_in,
  output [3:0] Sum,
  output C_out
);

  wire twobitadder_1_c_out;

  TwoBitAdder twobitadder_1 (.A(A[1:0]), .B(B[1:0]), .C_in(C_in), .Sum(Sum[1:0]), .C_out(twobitadder_1_c_out));
  TwoBitAdder twobitadder_2 (.A(A[3:2]), .B(B[3:2]), .C_in(twobitadder_1_c_out), .Sum(Sum[3:2]), .C_out(C_out));
endmodule

module EightBitAdder (
  input  [7:0] A,
  input  [7:0] B,
  input  C_in,
  output [7:0] Sum,
  output C_out
);

  wire fourbitadder_1_c_out;

  FourBitAdder fourbitadder_1 (.A(A[3:0]), .B(B[3:0]), .C_in(C_in), .Sum(Sum[3:0]), .C_out(fourbitadder_1_c_out));
  FourBitAdder fourbitadder_2 (.A(A[7:4]), .B(B[7:4]), .C_in(fourbitadder_1_c_out), .Sum(Sum[7:4]), .C_out(C_out));
endmodule

module SixteenBitAdder (
  input  [15:0] A,
  input  [15:0] B,
  input  C_in,
  output [15:0] Sum,
  output C_out
);

  wire eightbitadder_1_c_out;

  EightBitAdder eightbitadder_1 (.A(A[7:0]), .B(B[7:0]), .C_in(C_in), .Sum(Sum[7:0]), .C_out(eightbitadder_1_c_out));
  EightBitAdder eightbitadder_2 (
    .A(A[15:8]), .B(B[15:8]), .C_in(eightbitadder_1_c_out), .Sum(Sum[15:8]), .C_out(C_out));
endmodule

module SixteenBitSubtractor (
  input  [15:0] A,
  input  [15:0] B,
  output [15:0] out_3,
  output borrow_out
);

  wire [15:0] not_1_out;

  assign not_1_out = ~B;  // NOT_Gate not_1, 16 bits wide
  SixteenBitAdder sixteenbitadder_1 (.A(A), .B(not_1_out), .C_in(1'b1), .Sum(out_3), .C_out(borrow_out));
endmodule

module SixteenBitIncrement (
  input  [15:0] A,
  output [15:0] Increment
);

  SixteenBitAdder sixteenbitadder_1 (.A(A), .B({16{1'b0}}), .C_in(1'b1), .Sum(Increment));  // open: C_out
endmodule

module SixteenBitDecrement (
  input  [15:0] A,
  output [15:0] Decrement
);

  SixteenBitSubtractor sixteenbitsubtractor_1 (.A(A), .B(16'h1), .out_3(Decrement));  // open: borrow_out
endmodule

module Enabled_D_FlipFlop (
  input  D,
  input  clk,
  input  Enable,
  output Q,
  output Q_not
);

  wire multiplexer_1_out;

  Multiplexer multiplexer_1 (.in0(Q), .in1(D), .out(multiplexer_1_out), .sel(Enable));
  D_Flip_Flop d_ff_1 (.D(multiplexer_1_out), .clk(clk), .Q(Q), .Qn(Q_not));  // open: preset, reset
endmodule

module MyRegister (
  input  [7:0] input_bits,
  input  clk,
  input  enable,
  output [7:0] output_bits
);

  Enabled_D_FlipFlop enabled_d_flipflop_1 (
    .D(input_bits[0]), .clk(clk), .Enable(enable), .Q(output_bits[0]));  // open: Q_not
  Enabled_D_FlipFlop enabled_d_flipflop_2 (
    .D(input_bits[1]), .clk(clk), .Enable(enable), .Q(output_bits[1]));  // open: Q_not
  Enabled_D_FlipFlop enabled_d_flipflop_3 (
    .D(input_bits[2]), .clk(clk), .Enable(enable), .Q(output_bits[2]));  // open: Q_not
  Enabled_D_FlipFlop enabled_d_flipflop_4 (
    .D(input_bits[3]), .clk(clk), .Enable(enable), .Q(output_bits[3]));  // open: Q_not
  Enabled_D_FlipFlop enabled_d_flipflop_5 (
    .D(input_bits[4]), .clk(clk), .Enable(enable), .Q(output_bits[4]));  // open: Q_not
  Enabled_D_FlipFlop enabled_d_flipflop_6 (
    .D(input_bits[5]), .clk(clk), .Enable(enable), .Q(output_bits[5]));  // open: Q_not
  Enabled_D_FlipFlop enabled_d_flipflop_7 (
    .D(input_bits[6]), .clk(clk), .Enable(enable), .Q(output_bits[6]));  // open: Q_not
  Enabled_D_FlipFlop enabled_d_flipflop_8 (
    .D(input_bits[7]), .clk(clk), .Enable(enable), .Q(output_bits[7]));  // open: Q_not
endmodule

module Sixteen_Bit_Register (
  input  [15:0] input_bits,
  input  clk,
  input  enable,
  output [15:0] out_4
);

  MyRegister myregister_1 (.input_bits(input_bits[7:0]), .clk(clk), .enable(enable), .output_bits(out_4[7:0]));
  MyRegister myregister_2 (.input_bits(input_bits[15:8]), .clk(clk), .enable(enable), .output_bits(out_4[15:8]));
endmodule

module Twelve_Bit_Register (
  input  [11:0] input_bits,
  input  clk,
  input  LD,
  output [11:0] output_bits
);

  Enabled_D_FlipFlop enabled_d_flipflop_1 (
    .D(input_bits[0]), .clk(clk), .Enable(LD), .Q(output_bits[0]));  // open: Q_not
  Enabled_D_FlipFlop enabled_d_flipflop_2 (
    .D(input_bits[1]), .clk(clk), .Enable(LD), .Q(output_bits[1]));  // open: Q_not
  Enabled_D_FlipFlop enabled_d_flipflop_3 (
    .D(input_bits[2]), .clk(clk), .Enable(LD), .Q(output_bits[2]));  // open: Q_not
  Enabled_D_FlipFlop enabled_d_flipflop_4 (
    .D(input_bits[3]), .clk(clk), .Enable(LD), .Q(output_bits[3]));  // open: Q_not
  Enabled_D_FlipFlop enabled_d_flipflop_5 (
    .D(input_bits[4]), .clk(clk), .Enable(LD), .Q(output_bits[4]));  // open: Q_not
  Enabled_D_FlipFlop enabled_d_flipflop_6 (
    .D(input_bits[5]), .clk(clk), .Enable(LD), .Q(output_bits[5]));  // open: Q_not
  Enabled_D_FlipFlop enabled_d_flipflop_7 (
    .D(input_bits[6]), .clk(clk), .Enable(LD), .Q(output_bits[6]));  // open: Q_not
  Enabled_D_FlipFlop enabled_d_flipflop_8 (
    .D(input_bits[7]), .clk(clk), .Enable(LD), .Q(output_bits[7]));  // open: Q_not
  Enabled_D_FlipFlop enabled_d_flipflop_9 (
    .D(input_bits[8]), .clk(clk), .Enable(LD), .Q(output_bits[8]));  // open: Q_not
  Enabled_D_FlipFlop enabled_d_flipflop_10 (
    .D(input_bits[9]), .clk(clk), .Enable(LD), .Q(output_bits[9]));  // open: Q_not
  Enabled_D_FlipFlop enabled_d_flipflop_11 (
    .D(input_bits[10]), .clk(clk), .Enable(LD), .Q(output_bits[10]));  // open: Q_not
  Enabled_D_FlipFlop enabled_d_flipflop_12 (
    .D(input_bits[11]), .clk(clk), .Enable(LD), .Q(output_bits[11]));  // open: Q_not
endmodule

module TwoxFour_Decoder (
  input  [1:0] select_bits,
  input  enable,
  output [3:0] out_3
);

  wire not_1_out, not_2_out;

  not not_1 (not_1_out, select_bits[0]);
  not not_2 (not_2_out, select_bits[1]);
  and and_1 (out_3[0], not_2_out, not_1_out, enable);
  and and_2 (out_3[1], select_bits[0], not_2_out, enable);
  and and_3 (out_3[2], select_bits[1], not_1_out, enable);
  and and_4 (out_3[3], select_bits[1], select_bits[0], enable);
endmodule

module ThreebyEight_Decoder (
  input  [2:0] select_bits,
  input  enable,
  output [7:0] output_bits
);

  wire and_1_out, and_2_out, not_1_out;

  not not_1 (not_1_out, select_bits[2]);
  and and_1 (and_1_out, not_1_out, enable);
  and and_2 (and_2_out, select_bits[2], enable);
  TwoxFour_Decoder twoxfour_decoder_1 (.select_bits(select_bits[1:0]), .enable(and_1_out), .out_3(output_bits[3:0]));
  TwoxFour_Decoder twoxfour_decoder_2 (.select_bits(select_bits[1:0]), .enable(and_2_out), .out_3(output_bits[7:4]));
endmodule

module FourbySixteen_Decoder (
  input  [3:0] in_1,
  input  enable,
  output [15:0] out_3
);

  wire and_1_out, and_2_out, not_1_out;

  not not_1 (not_1_out, in_1[3]);
  and and_1 (and_1_out, in_1[3], enable);
  and and_2 (and_2_out, not_1_out, enable);
  ThreebyEight_Decoder threebyeight_decoder_1 (.select_bits(in_1[2:0]), .enable(and_2_out), .output_bits(out_3[7:0]));
  ThreebyEight_Decoder threebyeight_decoder_2 (.select_bits(in_1[2:0]), .enable(and_1_out), .output_bits(out_3[15:8]));
endmodule

module Left_Right_Shifter (
  input  [15:0] A,
  input  [1:0] mode,
  output [15:0] out_3
);

  wire clock_1_out, multiplexer_1_out, multiplexer_2_out, multiplexer_3_out, multiplexer_4_out,
       multiplexer_5_out, multiplexer_6_out, multiplexer_7_out, multiplexer_8_out, multiplexer_9_out,
       multiplexer_10_out, multiplexer_11_out, multiplexer_12_out, multiplexer_13_out, multiplexer_14_out,
       multiplexer_15_out, multiplexer_16_out;

  Clock clock_1 (.out(clock_1_out));
  Multiplexer #(.select(2)) multiplexer_1 (
    .in0(out_3[0]), .in1(A[0]), .in2(out_3[1]), .in3(1'b0), .out(multiplexer_1_out), .sel(mode));
  Multiplexer #(.select(2)) multiplexer_2 (
    .in0(out_3[1]), .in1(A[1]), .in2(out_3[2]), .in3(out_3[0]), .out(multiplexer_2_out), .sel(mode));
  Multiplexer #(.select(2)) multiplexer_3 (
    .in0(out_3[2]), .in1(A[2]), .in2(out_3[3]), .in3(out_3[1]), .out(multiplexer_3_out), .sel(mode));
  Multiplexer #(.select(2)) multiplexer_4 (
    .in0(out_3[3]), .in1(A[3]), .in2(out_3[4]), .in3(out_3[2]), .out(multiplexer_4_out), .sel(mode));
  Multiplexer #(.select(2)) multiplexer_5 (
    .in0(out_3[4]), .in1(A[4]), .in2(out_3[5]), .in3(out_3[3]), .out(multiplexer_5_out), .sel(mode));
  Multiplexer #(.select(2)) multiplexer_6 (
    .in0(out_3[5]), .in1(A[5]), .in2(out_3[6]), .in3(out_3[4]), .out(multiplexer_6_out), .sel(mode));
  Multiplexer #(.select(2)) multiplexer_7 (
    .in0(out_3[6]), .in1(A[6]), .in2(out_3[7]), .in3(out_3[5]), .out(multiplexer_7_out), .sel(mode));
  Multiplexer #(.select(2)) multiplexer_8 (
    .in0(out_3[7]), .in1(A[7]), .in2(out_3[8]), .in3(out_3[6]), .out(multiplexer_8_out), .sel(mode));
  Multiplexer #(.select(2)) multiplexer_9 (
    .in0(out_3[8]), .in1(A[8]), .in2(out_3[9]), .in3(out_3[7]), .out(multiplexer_9_out), .sel(mode));
  Multiplexer #(.select(2)) multiplexer_10 (
    .in0(out_3[10]), .in1(A[10]), .in2(out_3[11]), .in3(out_3[9]), .out(multiplexer_10_out), .sel(mode));
  Multiplexer #(.select(2)) multiplexer_11 (
    .in0(out_3[11]), .in1(A[11]), .in2(out_3[12]), .in3(out_3[10]), .out(multiplexer_11_out), .sel(mode));
  Multiplexer #(.select(2)) multiplexer_12 (
    .in0(out_3[12]), .in1(A[12]), .in2(out_3[13]), .in3(out_3[11]), .out(multiplexer_12_out), .sel(mode));
  Multiplexer #(.select(2)) multiplexer_13 (
    .in0(out_3[13]), .in1(A[13]), .in2(out_3[14]), .in3(out_3[12]), .out(multiplexer_13_out), .sel(mode));
  Multiplexer #(.select(2)) multiplexer_14 (
    .in0(out_3[14]), .in1(A[14]), .in2(out_3[15]), .in3(out_3[13]), .out(multiplexer_14_out), .sel(mode));
  Multiplexer #(.select(2)) multiplexer_15 (
    .in0(out_3[15]), .in1(A[15]), .in2(1'b0), .in3(out_3[14]), .out(multiplexer_15_out), .sel(mode));
  Multiplexer #(.select(2)) multiplexer_16 (
    .in0(out_3[9]), .in1(A[9]), .in2(out_3[10]), .in3(out_3[8]), .out(multiplexer_16_out), .sel(mode));
  D_Flip_Flop d_ff_1 (.D(multiplexer_1_out), .clk(clock_1_out), .Q(out_3[0]));  // open: Qn, preset, reset
  D_Flip_Flop d_ff_2 (.D(multiplexer_2_out), .clk(clock_1_out), .Q(out_3[1]));  // open: Qn, preset, reset
  D_Flip_Flop d_ff_3 (.D(multiplexer_3_out), .clk(clock_1_out), .Q(out_3[2]));  // open: Qn, preset, reset
  D_Flip_Flop d_ff_4 (.D(multiplexer_4_out), .clk(clock_1_out), .Q(out_3[3]));  // open: Qn, preset, reset
  D_Flip_Flop d_ff_5 (.D(multiplexer_5_out), .clk(clock_1_out), .Q(out_3[4]));  // open: Qn, preset, reset
  D_Flip_Flop d_ff_6 (.D(multiplexer_6_out), .clk(clock_1_out), .Q(out_3[5]));  // open: Qn, preset, reset
  D_Flip_Flop d_ff_7 (.D(multiplexer_7_out), .clk(clock_1_out), .Q(out_3[6]));  // open: Qn, preset, reset
  D_Flip_Flop d_ff_8 (.D(multiplexer_8_out), .clk(clock_1_out), .Q(out_3[7]));  // open: Qn, preset, reset
  D_Flip_Flop d_ff_9 (.D(multiplexer_9_out), .clk(clock_1_out), .Q(out_3[8]));  // open: Qn, preset, reset
  D_Flip_Flop d_ff_10 (.D(multiplexer_16_out), .clk(clock_1_out), .Q(out_3[9]));  // open: Qn, preset, reset
  D_Flip_Flop d_ff_11 (.D(multiplexer_10_out), .clk(clock_1_out), .Q(out_3[10]));  // open: Qn, preset, reset
  D_Flip_Flop d_ff_12 (.D(multiplexer_11_out), .clk(clock_1_out), .Q(out_3[11]));  // open: Qn, preset, reset
  D_Flip_Flop d_ff_13 (.D(multiplexer_12_out), .clk(clock_1_out), .Q(out_3[12]));  // open: Qn, preset, reset
  D_Flip_Flop d_ff_14 (.D(multiplexer_13_out), .clk(clock_1_out), .Q(out_3[13]));  // open: Qn, preset, reset
  D_Flip_Flop d_ff_15 (.D(multiplexer_14_out), .clk(clock_1_out), .Q(out_3[14]));  // open: Qn, preset, reset
  D_Flip_Flop d_ff_16 (.D(multiplexer_15_out), .clk(clock_1_out), .Q(out_3[15]));  // open: Qn, preset, reset
endmodule

module Left_Right_Circular_Shifter (
  input  [15:0] A,
  input  [1:0] mode,
  input  clk,
  output [15:0] out_4
);

  wire multiplexer_1_out, multiplexer_2_out, multiplexer_3_out, multiplexer_4_out, multiplexer_5_out,
       multiplexer_6_out, multiplexer_7_out, multiplexer_8_out, multiplexer_9_out, multiplexer_10_out,
       multiplexer_11_out, multiplexer_12_out, multiplexer_13_out, multiplexer_14_out, multiplexer_15_out,
       multiplexer_16_out;

  Multiplexer #(.select(2)) multiplexer_1 (
    .in0(out_4[0]), .in1(A[0]), .in2(out_4[1]), .in3(out_4[15]), .out(multiplexer_1_out), .sel(mode));
  Multiplexer #(.select(2)) multiplexer_2 (
    .in0(out_4[1]), .in1(A[1]), .in2(out_4[2]), .in3(out_4[0]), .out(multiplexer_2_out), .sel(mode));
  Multiplexer #(.select(2)) multiplexer_3 (
    .in0(out_4[2]), .in1(A[2]), .in2(out_4[3]), .in3(out_4[1]), .out(multiplexer_3_out), .sel(mode));
  Multiplexer #(.select(2)) multiplexer_4 (
    .in0(out_4[3]), .in1(A[3]), .in2(out_4[4]), .in3(out_4[2]), .out(multiplexer_4_out), .sel(mode));
  Multiplexer #(.select(2)) multiplexer_5 (
    .in0(out_4[4]), .in1(A[4]), .in2(out_4[5]), .in3(out_4[3]), .out(multiplexer_5_out), .sel(mode));
  Multiplexer #(.select(2)) multiplexer_6 (
    .in0(out_4[5]), .in1(A[5]), .in2(out_4[6]), .in3(out_4[4]), .out(multiplexer_6_out), .sel(mode));
  Multiplexer #(.select(2)) multiplexer_7 (
    .in0(out_4[6]), .in1(A[6]), .in2(out_4[7]), .in3(out_4[5]), .out(multiplexer_7_out), .sel(mode));
  Multiplexer #(.select(2)) multiplexer_8 (
    .in0(out_4[7]), .in1(A[7]), .in2(out_4[8]), .in3(out_4[6]), .out(multiplexer_8_out), .sel(mode));
  Multiplexer #(.select(2)) multiplexer_9 (
    .in0(out_4[8]), .in1(A[8]), .in2(out_4[9]), .in3(out_4[7]), .out(multiplexer_9_out), .sel(mode));
  Multiplexer #(.select(2)) multiplexer_10 (
    .in0(out_4[10]), .in1(A[10]), .in2(out_4[11]), .in3(out_4[9]), .out(multiplexer_10_out), .sel(mode));
  Multiplexer #(.select(2)) multiplexer_11 (
    .in0(out_4[11]), .in1(A[11]), .in2(out_4[12]), .in3(out_4[10]), .out(multiplexer_11_out), .sel(mode));
  Multiplexer #(.select(2)) multiplexer_12 (
    .in0(out_4[12]), .in1(A[12]), .in2(out_4[13]), .in3(out_4[11]), .out(multiplexer_12_out), .sel(mode));
  Multiplexer #(.select(2)) multiplexer_13 (
    .in0(out_4[13]), .in1(A[13]), .in2(out_4[14]), .in3(out_4[12]), .out(multiplexer_13_out), .sel(mode));
  Multiplexer #(.select(2)) multiplexer_14 (
    .in0(out_4[14]), .in1(A[14]), .in2(out_4[15]), .in3(out_4[13]), .out(multiplexer_14_out), .sel(mode));
  Multiplexer #(.select(2)) multiplexer_15 (
    .in0(out_4[15]), .in1(A[15]), .in2(out_4[0]), .in3(out_4[14]), .out(multiplexer_15_out), .sel(mode));
  Multiplexer #(.select(2)) multiplexer_16 (
    .in0(out_4[9]), .in1(A[9]), .in2(out_4[10]), .in3(out_4[8]), .out(multiplexer_16_out), .sel(mode));
  D_Flip_Flop d_ff_1 (.D(multiplexer_1_out), .clk(clk), .Q(out_4[0]));  // open: Qn, preset, reset
  D_Flip_Flop d_ff_2 (.D(multiplexer_2_out), .clk(clk), .Q(out_4[1]));  // open: Qn, preset, reset
  D_Flip_Flop d_ff_3 (.D(multiplexer_3_out), .clk(clk), .Q(out_4[2]));  // open: Qn, preset, reset
  D_Flip_Flop d_ff_4 (.D(multiplexer_4_out), .clk(clk), .Q(out_4[3]));  // open: Qn, preset, reset
  D_Flip_Flop d_ff_5 (.D(multiplexer_5_out), .clk(clk), .Q(out_4[4]));  // open: Qn, preset, reset
  D_Flip_Flop d_ff_6 (.D(multiplexer_6_out), .clk(clk), .Q(out_4[5]));  // open: Qn, preset, reset
  D_Flip_Flop d_ff_7 (.D(multiplexer_7_out), .clk(clk), .Q(out_4[6]));  // open: Qn, preset, reset
  D_Flip_Flop d_ff_8 (.D(multiplexer_8_out), .clk(clk), .Q(out_4[7]));  // open: Qn, preset, reset
  D_Flip_Flop d_ff_9 (.D(multiplexer_9_out), .clk(clk), .Q(out_4[8]));  // open: Qn, preset, reset
  D_Flip_Flop d_ff_10 (.D(multiplexer_16_out), .clk(clk), .Q(out_4[9]));  // open: Qn, preset, reset
  D_Flip_Flop d_ff_11 (.D(multiplexer_10_out), .clk(clk), .Q(out_4[10]));  // open: Qn, preset, reset
  D_Flip_Flop d_ff_12 (.D(multiplexer_11_out), .clk(clk), .Q(out_4[11]));  // open: Qn, preset, reset
  D_Flip_Flop d_ff_13 (.D(multiplexer_12_out), .clk(clk), .Q(out_4[12]));  // open: Qn, preset, reset
  D_Flip_Flop d_ff_14 (.D(multiplexer_13_out), .clk(clk), .Q(out_4[13]));  // open: Qn, preset, reset
  D_Flip_Flop d_ff_15 (.D(multiplexer_14_out), .clk(clk), .Q(out_4[14]));  // open: Qn, preset, reset
  D_Flip_Flop d_ff_16 (.D(multiplexer_15_out), .clk(clk), .Q(out_4[15]));  // open: Qn, preset, reset
endmodule

module Reg12_LIC (
  input  [11:0] data,
  input  INR,
  input  clear,
  input  LD,
  input  clk,
  output [11:0] output_bits
);

  wire or_1_out;
  wire [11:0] adder_1_out, multiplexer_1_out, multiplexer_2_out;

  Multiplexer #(.width(12)) multiplexer_1 (.in0(data), .in1(adder_1_out), .out(multiplexer_1_out), .sel(INR));
  Multiplexer #(.width(12)) multiplexer_2 (
    .in0(multiplexer_1_out), .in1({12{1'b0}}), .out(multiplexer_2_out), .sel(clear));
  or or_1 (or_1_out, INR, clear, LD);
  Adder #(.width(12)) adder_1 (.a(12'h1), .b(output_bits), .out(adder_1_out));  // open: cin, cout
  Twelve_Bit_Register twelve_bit_register_1 (
    .input_bits(multiplexer_2_out), .clk(clk), .LD(or_1_out), .output_bits(output_bits));
endmodule

module Reg16_LIC (
  input  [15:0] data,
  input  INR,
  input  clear,
  input  LD,
  input  clk,
  output [15:0] output_bits
);

  wire or_1_out;
  wire [15:0] adder_1_out, multiplexer_1_out, multiplexer_2_out;

  Multiplexer #(.width(16)) multiplexer_1 (.in0(data), .in1(adder_1_out), .out(multiplexer_1_out), .sel(INR));
  Multiplexer #(.width(16)) multiplexer_2 (
    .in0(multiplexer_1_out), .in1({16{1'b0}}), .out(multiplexer_2_out), .sel(clear));
  or or_1 (or_1_out, INR, clear, LD);
  Adder #(.width(16)) adder_1 (.a(16'h1), .b(output_bits), .out(adder_1_out));  // open: cin, cout
  Sixteen_Bit_Register sixteen_bit_register_1 (
    .input_bits(multiplexer_2_out), .clk(clk), .enable(or_1_out), .out_4(output_bits));
endmodule

module AR (
  input  [11:0] D,
  input  INR,
  input  clear,
  input  LD,
  input  clk,
  output [11:0] output_bits
);

  Reg12_LIC reg12_lic_1 (.data(D), .INR(INR), .clear(clear), .LD(LD), .clk(clk), .output_bits(output_bits));
endmodule

module PC (
  input  [11:0] D,
  input  INR,
  input  clear,
  input  LD,
  input  clk,
  output [11:0] output_bits
);

  Reg12_LIC reg12_lic_1 (.data(D), .INR(INR), .clear(clear), .LD(LD), .clk(clk), .output_bits(output_bits));
endmodule

module DR (
  input  [15:0] D,
  input  INR,
  input  LD,
  input  clk,
  output [15:0] output_bits
);

  Reg16_LIC reg16_lic_1 (.data(D), .INR(INR), .clear(1'b0), .LD(LD), .clk(clk), .output_bits(output_bits));
endmodule

module AC (
  input  [15:0] D,
  input  INR,
  input  clear,
  input  LD,
  input  clk,
  output [15:0] output_bits
);

  Reg16_LIC reg16_lic_1 (.data(D), .INR(INR), .clear(clear), .LD(LD), .clk(clk), .output_bits(output_bits));
endmodule

module IR (
  input  [15:0] D,
  input  LD,
  input  clk,
  output [15:0] output_bits
);

  Sixteen_Bit_Register sixteen_bit_register_1 (.input_bits(D), .clk(clk), .enable(LD), .out_4(output_bits));
endmodule

module TR (
  input  [15:0] D,
  input  LD,
  input  clk,
  output [15:0] output_bits
);

  Sixteen_Bit_Register sixteen_bit_register_1 (.input_bits(D), .clk(clk), .enable(LD), .out_4(output_bits));
endmodule

module SC (
  input  INR,
  input  clear,
  input  clk,
  output [3:0] output_bits
);

  wire and_1_out, and_2_out, and_3_out, multiplexer_1_out, multiplexer_2_out, multiplexer_3_out,
       multiplexer_4_out;

  Multiplexer multiplexer_1 (.in0(INR), .in1(output_bits[0]), .out(multiplexer_1_out), .sel(clear));
  T_Flip_Flop t_ff_1 (.T(multiplexer_1_out), .clk(clk), .Q(output_bits[0]));  // open: Qn, reset, preset
  and and_1 (and_1_out, INR, output_bits[0]);
  Multiplexer multiplexer_2 (.in0(and_1_out), .in1(output_bits[1]), .out(multiplexer_2_out), .sel(clear));
  T_Flip_Flop t_ff_2 (.T(multiplexer_2_out), .clk(clk), .Q(output_bits[1]));  // open: Qn, reset, preset
  and and_2 (and_2_out, and_1_out, output_bits[1]);
  Multiplexer multiplexer_3 (.in0(and_2_out), .in1(output_bits[2]), .out(multiplexer_3_out), .sel(clear));
  T_Flip_Flop t_ff_3 (.T(multiplexer_3_out), .clk(clk), .Q(output_bits[2]));  // open: Qn, reset, preset
  and and_3 (and_3_out, and_2_out, output_bits[2]);
  Multiplexer multiplexer_4 (.in0(and_3_out), .in1(output_bits[3]), .out(multiplexer_4_out), .sel(clear));
  T_Flip_Flop t_ff_4 (.T(multiplexer_4_out), .clk(clk), .Q(output_bits[3]));  // open: Qn, reset, preset
endmodule

module SP (
  input  INR,
  input  DCR,
  input  INIT,
  input  clk,
  output [11:0] SP_out
);

  wire or_1_out;
  wire [11:0] adder_1_out, adder_2_out, multiplexer_1_out, multiplexer_2_out;

  Multiplexer #(.width(12)) multiplexer_1 (.in0(adder_1_out), .in1(adder_2_out), .out(multiplexer_1_out), .sel(INR));
  Multiplexer #(.width(12)) multiplexer_2 (
    .in0(multiplexer_1_out), .in1({12{1'b1}}), .out(multiplexer_2_out), .sel(INIT));
  or or_1 (or_1_out, INIT, INR, DCR);
  Twelve_Bit_Register twelve_bit_register_1 (
    .input_bits(multiplexer_2_out), .clk(clk), .LD(or_1_out), .output_bits(SP_out));
  Adder #(.width(12)) adder_1 (.a({12{1'b1}}), .b(SP_out), .out(adder_1_out));  // open: cin, cout
  Adder #(.width(12)) adder_2 (.a(12'h1), .b(SP_out), .out(adder_2_out));  // open: cin, cout
endmodule

module Common_Bus (
  input  [11:0] SP,
  input  [11:0] AR,
  input  [11:0] PC,
  input  [15:0] DR,
  input  [15:0] AC,
  input  [15:0] IR,
  input  [15:0] TR,
  input  [15:0] MEM,
  input  [2:0] Sel,
  output [15:0] My_Bus
);

  wire [7:0] threebyeight_decoder_1_output_bits;
  wire [15:0] and_1_out, and_2_out, and_3_out, and_4_out, and_5_out, and_6_out, and_7_out, and_8_out,
       bit_extender_1_out, bit_extender_2_out, bit_extender_3_out, bit_extender_4_out, bit_extender_5_out,
       bit_extender_6_out, bit_extender_7_out, bit_extender_8_out, bit_extender_9_out, bit_extender_10_out,
       bit_extender_11_out;

  ThreebyEight_Decoder threebyeight_decoder_1 (
    .select_bits(Sel), .enable(1'b1), .output_bits(threebyeight_decoder_1_output_bits));
  assign bit_extender_1_out = {{4{1'b0}}, SP};  // Bit_Extender bit_extender_1
  assign bit_extender_2_out = {{15{threebyeight_decoder_1_output_bits[0]}}, threebyeight_decoder_1_output_bits[0]};  // Bit_Extender bit_extender_2
  assign bit_extender_3_out = {{15{threebyeight_decoder_1_output_bits[6]}}, threebyeight_decoder_1_output_bits[6]};  // Bit_Extender bit_extender_3
  assign bit_extender_4_out = {{15{threebyeight_decoder_1_output_bits[5]}}, threebyeight_decoder_1_output_bits[5]};  // Bit_Extender bit_extender_4
  assign bit_extender_5_out = {{15{threebyeight_decoder_1_output_bits[7]}}, threebyeight_decoder_1_output_bits[7]};  // Bit_Extender bit_extender_5
  assign bit_extender_6_out = {{4{1'b0}}, AR};  // Bit_Extender bit_extender_6
  assign bit_extender_7_out = {{15{threebyeight_decoder_1_output_bits[1]}}, threebyeight_decoder_1_output_bits[1]};  // Bit_Extender bit_extender_7
  assign bit_extender_8_out = {{4{1'b0}}, PC};  // Bit_Extender bit_extender_8
  assign bit_extender_9_out = {{15{threebyeight_decoder_1_output_bits[2]}}, threebyeight_decoder_1_output_bits[2]};  // Bit_Extender bit_extender_9
  assign bit_extender_10_out = {{15{threebyeight_decoder_1_output_bits[3]}}, threebyeight_decoder_1_output_bits[3]};  // Bit_Extender bit_extender_10
  assign bit_extender_11_out = {{15{threebyeight_decoder_1_output_bits[4]}}, threebyeight_decoder_1_output_bits[4]};  // Bit_Extender bit_extender_11
  assign and_1_out = TR & bit_extender_3_out;  // AND_Gate and_1, 16 bits wide
  assign and_2_out = bit_extender_1_out & bit_extender_2_out;  // AND_Gate and_2, 16 bits wide
  assign and_3_out = IR & bit_extender_4_out;  // AND_Gate and_3, 16 bits wide
  assign and_4_out = MEM & bit_extender_5_out;  // AND_Gate and_4, 16 bits wide
  assign and_5_out = bit_extender_6_out & bit_extender_7_out;  // AND_Gate and_5, 16 bits wide
  assign and_6_out = bit_extender_8_out & bit_extender_9_out;  // AND_Gate and_6, 16 bits wide
  assign and_7_out = DR & bit_extender_10_out;  // AND_Gate and_7, 16 bits wide
  assign and_8_out = AC & bit_extender_11_out;  // AND_Gate and_8, 16 bits wide
  assign My_Bus = and_2_out | and_5_out | and_6_out | and_7_out | and_3_out | and_1_out | and_4_out | and_8_out;  // OR_Gate or_1, 16 bits wide
endmodule

module CPU_With_Bus (
  input  in_1,
  input  start,
  input  [7:0] KBD_data,
  input  in_4,
  input  key,
  input  ready,
  output [15:0] out_7,
  output [15:0] out_8,
  output [11:0] out_9,
  output [11:0] out_10,
  output [15:0] out_11,
  output out_12,
  output [7:0] printer,
  output [15:0] out_14,
  output [15:0] out_15,
  output out_16,
  output out_17,
  output [15:0] out_18,
  output out_19,
  output [15:0] out_20,
  output [11:0] out_21
);

  wire AC_LD, AC_zero, and_2_out, and_3_out, and_4_out, and_5_out, and_10_out, and_11_out, and_12_out,
       and_13_out, and_14_out, and_15_out, and_16_out, and_17_out, and_18_out, and_22_out, and_23_out,
       and_35_out, and_36_out, and_39_out, and_40_out, and_53_out, and_54_out, and_55_out, and_56_out,
       and_63_out, and_64_out, and_65_out, and_66_out, and_67_out, and_68_out, and_69_out, and_70_out,
       and_71_out, and_72_out, and_73_out, and_74_out, and_75_out, and_76_out, and_77_out, and_78_out,
       and_79_out, and_80_out, and_81_out, and_82_out, AR_LD, Arithmetic_Logic_Unit_p7, clk, D0, D1, D2, D3,
       D4, D5, D5T4, D5T6, D5T7, D6, D7, DR_INR, DR_LD, DR_zero, E_q, Increment_Counter, Ind_Cycle, Indirect,
       MemRd, not_1_out, not_2_out, not_3_out, not_4_out, not_5_out, not_6_out, not_7_out, not_8_out,
       not_9_out, not_10_out, not_11_out, not_12_out, not_13_out, or_1_out, or_4_out, or_5_out, or_12_out,
       or_13_out, or_14_out, or_15_out, or_20_out, or_21_out, or_22_out, or_23_out, or_24_out, p, pB6, pB7,
       pB8, pB9, pB10, pB11, PC_from_AR, PC_INR, PC_LD, Po, PoT3, PoT4, PoT5, Pu, PuT3, PuT4, PuT5, r,
       RAM_write_enable, rB0, rB1, rB2, rB3, rB4, rB5, rB6, rB7, rB8, rB9, rB10, rB11, Re, ReT3, ReT4,
       RNot_T0, RNot_T1, RNot_T2, S0, S1, S2, SC_clear, T0, T1, T2, T3, T4, T5, T6, T7, T8, T9, T10, T11,
       T12, T13, T14, T15;
  wire [2:0] or_16_out;
  wire [3:0] sc_1_output_bits;
  wire [7:0] INPR_out;

  not not_1 (not_1_out, D7);
  not not_2 (not_2_out, r);
  and and_1 (Ind_Cycle, T3, Indirect, not_1_out);
  and and_2 (and_2_out, D0, T4);
  and and_3 (and_3_out, T4, D1);
  and and_4 (and_4_out, T4, D2);
  and and_5 (and_5_out, T4, D6);
  and and_6 (DR_INR, D6, T5);
  and and_7 (RNot_T0, T0, not_2_out);
  and and_8 (RNot_T1, not_2_out, T1);
  and and_9 (RNot_T2, not_2_out, T2);
  and and_10 (and_10_out, T4, D5);
  or or_1 (or_1_out, PuT3, D5T4);
  or or_2 (AR_LD, ReT3, PuT4, RNot_T0, D5T6, RNot_T2, Ind_Cycle, PoT3);
  or or_3 (MemRd, and_2_out, and_3_out, and_4_out, and_5_out);
  or or_4 (or_4_out, out_7[3], out_7[4], out_7[5]);
  and and_11 (and_11_out, D0, T5);
  and and_12 (and_12_out, D1, T5);
  and and_13 (and_13_out, D2, T5);
  and and_14 (and_14_out, D3, T4);
  and and_15 (and_15_out, D4, T4);
  and and_16 (and_16_out, D5, T7);
  and and_17 (and_17_out, D6, T6);
  or or_5 (or_5_out, ReT4, PoT4);
  not not_3 (not_3_out, or_4_out);
  or or_6 (DR_LD, PoT4, MemRd, and_10_out);
  and and_18 (and_18_out, not_3_out, p);
  and and_19 (Re, D7, Indirect, out_7[3]);
  and and_20 (Po, D7, Indirect, out_7[4]);
  and and_21 (Pu, Indirect, D7, out_7[5]);
  PC Program_Counter (.D(out_20[11:0]), .INR(PC_INR), .clear(in_4), .LD(PC_LD), .clk(clk), .output_bits(out_9));
  and and_22 (and_22_out, D4, T4);
  and and_23 (and_23_out, D5, T5);
  or or_7 (SC_clear, PoT5, and_18_out, r, and_11_out, and_12_out, and_13_out, and_16_out, and_14_out, and_15_out, in_1, and_17_out, rB0, PuT5, ReT4);
  SP sp_1 (.INR(or_5_out), .DCR(or_1_out), .INIT(start), .clk(clk), .SP_out(out_21));
  or or_8 (PC_from_AR, and_22_out, and_23_out);
  SC sc_1 (.INR(Increment_Counter), .clear(SC_clear), .clk(clk), .output_bits(sc_1_output_bits));
  ThreebyEight_Decoder threebyeight_decoder_1 (
    .select_bits(out_7[14:12]), .enable(1'b1), .output_bits({D7, D6, D5, D4, D3, D2, D1, D0}));
  or or_9 (PC_LD, PC_from_AR, ReT4);
  and and_24 (D5T6, T6, D5);
  and and_25 (D5T7, T7, D5);
  and and_26 (D5T4, T4, D5);
  FourbySixteen_Decoder fourbysixteen_decoder_1 (
    .in_1(sc_1_output_bits), .enable(1'b1),
    .out_3({T15, T14, T13, T12, T11, T10, T9, T8, T7, T6, T5, T4, T3, T2, T1, T0}));
  and and_27 (ReT3, Re, T3);
  and and_28 (ReT4, Re, T4);
  and and_29 (PoT3, Po, T3);
  and and_30 (PoT4, Po, T4);
  and and_31 (PoT5, Po, T5);
  and and_32 (PuT3, Pu, T3);
  and and_33 (PuT4, Pu, T4);
  and and_34 (PuT5, Pu, T5);
  not not_4 (not_4_out, Indirect);
  Clock clock_1 (.out(clk));
  AR Address_Register (.D(out_20[11:0]), .INR(1'b0), .clear(1'b0), .LD(AR_LD), .clk(clk), .output_bits(out_10));
  and and_35 (and_35_out, D3, T4);
  and and_36 (and_36_out, D6, T6);
  and and_37 (r, D7, not_4_out, T3);
  and and_38 (p, D7, Indirect, T3);
  and and_39 (and_39_out, D0, T5);
  and and_40 (and_40_out, D1, T5);
  and and_41 (rB0, r, out_7[0]);
  and and_42 (rB1, r, out_7[1]);
  and and_43 (rB2, r, out_7[2]);
  and and_44 (rB3, r, out_7[3]);
  and and_45 (rB4, r, out_7[4]);
  and and_46 (rB5, r, out_7[5]);
  and and_47 (rB6, r, out_7[6]);
  and and_48 (rB7, r, out_7[7]);
  and and_49 (rB8, r, out_7[8]);
  and and_50 (rB9, r, out_7[9]);
  and and_51 (rB10, r, out_7[10]);
  and and_52 (rB11, r, out_7[11]);
  not not_5 (not_5_out, start);
  RAM #(.addrWidth(12), .asyncread("true"), .dataWidth(16)) ram_1 (
    .addr(out_10), .we(RAM_write_enable), .oe(1'b1), .clk(clk), .din(out_20), .dout(out_11));
  and and_53 (and_53_out, D2, T5);
  or or_10 (RAM_write_enable, PuT5, and_35_out, D5T7, and_36_out);
  and and_54 (and_54_out, not_5_out, rB0);
  J_K_Flip_Flop j_k_ff_1 (.J(start), .K(and_54_out), .clk(clk), .Q(Increment_Counter));  // open: Qn, preset, reset
  or or_11 (AC_LD, PoT5, and_39_out, and_40_out, and_53_out, rB6, rB7, rB9, pB11);
  or or_12 (or_12_out, rB10, rB8);
  not not_6 (not_6_out, or_12_out);
  not not_7 (not_7_out, E_q);
  and and_55 (and_55_out, Arithmetic_Logic_Unit_p7, not_6_out);
  and and_56 (and_56_out, rB8, not_7_out);
  IR Instruction_Register (.D(out_20), .LD(RNot_T1), .clk(clk), .output_bits(out_7));
  or or_13 (or_13_out, and_55_out, and_56_out);
  and and_57 (pB6, p, out_7[6]);
  and and_58 (pB7, p, out_7[7]);
  and and_59 (pB8, p, out_7[8]);
  and and_60 (pB9, p, out_7[9]);
  and and_61 (pB10, p, out_7[10]);
  and and_62 (pB11, p, out_7[11]);
  and and_63 (and_63_out, D1, T5);
  and and_64 (and_64_out, or_13_out, or_14_out);
  not not_8 (not_8_out, or_13_out);
  and and_65 (and_65_out, not_8_out, or_14_out);
  not not_9 (not_9_out, E_q);
  DR Data_Register (.D(out_20), .INR(DR_INR), .LD(DR_LD), .clk(clk), .output_bits(out_14));
  AC Accumulator (.D(out_15), .INR(rB5), .clear(rB11), .LD(AC_LD), .clk(clk), .output_bits(out_18));
  J_K_Flip_Flop E (.J(and_64_out), .K(and_65_out), .clk(clk), .Q(E_q));  // open: Qn, preset, reset
  or or_14 (or_14_out, and_63_out, rB10, rB8, rB7, rB6);
  not not_10 (not_10_out, out_18[15]);
  and and_66 (and_66_out, out_7[3], out_18[15]);
  and and_67 (and_67_out, out_7[2], AC_zero);
  and and_68 (and_68_out, out_7[4], not_10_out);
  and and_69 (and_69_out, out_7[1], not_9_out);
  or or_15 (or_15_out, and_68_out, and_66_out, and_67_out, and_69_out);
  or or_16 (or_16_out[0], D1, rB9, rB6);
  or or_17 (or_16_out[1], D2, pB11, PoT5, rB9);
  and and_70 (and_70_out, r, or_15_out);
  not not_11 (not_11_out, out_7[15]);
  or or_18 (or_16_out[2], rB7, pB11, rB6);
  and and_71 (and_71_out, D6, T6, DR_zero);
  and and_72 (and_72_out, RNot_T2, out_7[15]);
  and and_73 (and_73_out, RNot_T2, not_11_out);
  and and_74 (and_74_out, out_16, pB9);
  and and_75 (and_75_out, out_17, pB8);
  J_K_Flip_Flop j_k_ff_2 (.J(and_72_out), .K(and_73_out), .clk(clk), .Q(Indirect));  // open: Qn, preset, reset
  or or_19 (PC_INR, and_71_out, and_74_out, RNot_T1, and_75_out, and_70_out);
  nor nor_1 (DR_zero, out_14[0], out_14[1], out_14[2], out_14[3], out_14[4], out_14[5], out_14[6], out_14[7], out_14[8], out_14[9], out_14[10], out_14[11], out_14[12], out_14[13], out_14[14], out_14[15]);
  // ALU Arithmetic_Logic_Unit: pin names not known; wires that end beside it: out_18, out_14, E_q, INPR_out, or_16_out, out_15, Arithmetic_Logic_Unit_p7
  nor nor_2 (AC_zero, out_18[0], out_18[1], out_18[2], out_18[3], out_18[4], out_18[5], out_18[6], out_18[7], out_18[8], out_18[9], out_18[10], out_18[11], out_18[12], out_18[13], out_18[14], out_18[15]);
  not not_12 (not_12_out, key);
  not not_13 (not_13_out, ready);
  and and_76 (and_76_out, not_12_out, pB11);
  and and_77 (and_77_out, not_13_out, pB10);
  J_K_Flip_Flop FGI (.J(key), .K(and_76_out), .clk(clk), .Q(out_16));  // open: Qn, preset, reset
  J_K_Flip_Flop FGO (.J(ready), .K(and_77_out), .clk(clk), .Q(out_17));  // open: Qn, preset, reset
  J_K_Flip_Flop IEN (.J(pB7), .K(pB6), .clk(clk), .Q(out_19));  // open: Qn, preset, reset
  and and_78 (and_78_out, D5, T7);
  // INPR inpr_1: pin names not known; wires that end beside it: KBD_data, key, clk, INPR_out
  // OUTR outr_1: pin names not known; wires that end beside it: out_20[7:0], pB10, clk, printer
  Common_Bus common_bus_1 (
    .SP(out_21), .AR(out_10), .PC(out_9), .DR(out_14), .AC(out_18), .IR(out_7), .TR({16{1'b0}}),
    .MEM(out_11), .Sel({S2, S1, S0}), .My_Bus(out_20));
  and and_79 (and_79_out, D3, T4);
  and and_80 (and_80_out, D6, T6);
  and and_81 (and_81_out, D5, T4);
  and and_82 (and_82_out, D6, T6);
  or or_20 (or_20_out, and_81_out, RNot_T0);
  or or_21 (or_21_out, and_80_out, and_78_out);
  or or_22 (or_22_out, RNot_T1, ReT4, MemRd, PoT4, Ind_Cycle);
  or or_23 (or_23_out, and_78_out, and_82_out);
  or or_24 (or_24_out, and_79_out, PuT5, pB10);
  or or_25 (S0, PC_from_AR, or_21_out, RNot_T2, or_22_out);
  or or_26 (S1, or_20_out, or_23_out, 1'b0, or_22_out);
  or or_27 (S2, or_24_out, RNot_T2, 1'b0, or_22_out);

  assign out_8 = out_7;
  assign out_12 = out_7[15];

  // Other names for the same wires on the sheet: AC_0_7[7:0] = {out_18[7], out_18[2], out_18[5:0]};
  //   AC_out[15:0] = out_18; AC_D[15:0] = out_15; AC_15 = out_18[15]; AR_out[11:0] = out_10;
  //   BUS_0_7[7:0] = out_20[7:0]; BUS_0_11[11:0] = out_20[11:0]; My_Bus[15:0] = out_20; DR_out[15:0] = out_14;
  //   FGI_out = out_16; FGO_out = out_17; Interrupt_Enabled = out_19; B0 = out_7[0]; IR_addr[11:0] = out_7[11:0];
  //   IR_out[15:0] = out_7; B1 = out_7[1]; B2 = out_7[2]; B3 = out_7[3]; B4 = out_7[4]; B5 = out_7[5]; B6 = out_7[6];
  //   B7 = out_7[7]; B8 = out_7[8]; B9 = out_7[9]; B10 = out_7[10]; B11 = out_7[11]; OP_Code[2:0] = out_7[14:12];
  //   IR15 = out_7[15]; Mem0_11[11:0] = out_11[11:0]; Mem_out[15:0] = out_11; PC_out[11:0] = out_9;
  //   Reset_Counter = in_1; SP_out[11:0] = out_21
endmodule
